# Fritzing sketch Diagrama eléctrico Único (saved by Fritzing 0.9.2b)
breadboards: 1

parts:
  Raspberry_Pi_1 = Raspberry Pi 3 [part_number=RPI-3-V1.2]  # not connected
  Part1 = Arduino Mega 2560 (Rev3)
  U1 = LIPO-2000mAh [package=lipo-2000]
  U2 = LIPO-2000mAh [package=lipo-2000]
  Stepdown_Voltage1 = Polulu Stepdown Voltage [part_number=D24V25F3,D24V25F5]
  X1 = USB Connectors [package=usb-microb]
  U4 = USB+SHIELD [package=usb-b-pth]
  X2 = USB Connectors [package=usb-a-h]
  MD03A1 = Dual VNH2SP30 Motor Driver [part_number=MD03A]
  X3 = USB Connectors [package=usb-minib]
  Part2 = LilyPad Coin Cell Battery Holder  # not connected
  X4 = USB Connectors [package=usb-a-s-silk-female]
  X6 = USB Connectors [package=usb-a-s-silk-female]
  X7 = USB Connectors [package=usb-a-s-silk-female]
  X8 = USB Connectors [package=usb-a-h]  # not connected
  X9 = USB Connectors [package=usb-a-h]
  X10 = USB Connectors [package=usb-a-h]
  DC_Mot_Enc1 = DC Motor with two-phase hall-encoder [part_number=VT-E-G25A-06-177E]
  R1 = Resistor [tolerance=±5% resistance=220 package=THT]  # not connected
  DC_Mot_Enc2 = DC Motor with two-phase hall-encoder [part_number=VT-E-G25A-06-177E]
  DC_Mot_Enc3 = DC Motor with two-phase hall-encoder [part_number=VT-E-G25A-06-177E]
  DC_Mot_Enc4 = DC Motor with two-phase hall-encoder [part_number=VT-E-G25A-06-177E]
  DC_Mot_Enc5 = DC Motor with two-phase hall-encoder [part_number=VT-E-G25A-06-177E]
  DC_Mot_Enc6 = DC Motor with two-phase hall-encoder [part_number=VT-E-G25A-06-177E]
  R10 = Resistor [tolerance=±5% resistance=220 package=THT]
  R11 = Photocell (LDR) [package=THT]
  R12 = Resistor [tolerance=±5% resistance=220 package=THT]
  R13 = Photocell (LDR) [package=THT]
  R14 = Resistor [tolerance=±5% resistance=220 package=THT]
  R15 = Photocell (LDR) [package=THT]
  R16 = Resistor [tolerance=±5% resistance=220 package=THT]
  R17 = Photocell (LDR) [package=THT]
  R18 = Resistor [tolerance=±5% resistance=220 package=THT]
  R19 = Photocell (LDR) [package=THT]
  R20 = Resistor [tolerance=±5% resistance=220 package=THT]
  R21 = Photocell (LDR) [package=THT]
  R22 = Resistor [tolerance=±5% resistance=220 package=THT]
  R23 = Photocell (LDR) [package=THT]
  R24 = Resistor [tolerance=±5% resistance=220 package=THT]
  R25 = Photocell (LDR) [package=THT]
  LED1 = LED - 5mm [color="Green (555nm)" package="5 mm [THT]"]
  LED2 = LED - 5mm [color="Green (555nm)" package="5 mm [THT]"]
  R26 = Resistor [tolerance=±5% resistance=220 package=THT]
  R27 = Resistor [tolerance=±5% resistance=220 package=THT]
  Part3 = Arduino Mega 2560 (Rev3)
  S1 = Toggle Switch spst [package=THT]
  R28 = Resistor [tolerance=±5% resistance=220 package=THT]  # not connected
  R29 = Resistor [tolerance=±5% resistance=220 package=THT]  # not connected
  R30 = Resistor [tolerance=±5% resistance=220 package=THT]  # not connected
  R31 = Resistor [tolerance=±5% resistance=220 package=THT]  # not connected

nets:
  N1: Part1.A0, R10.Pin_0, R11.pin_1
  N2: Part1.A1, R12.Pin_0, R13.pin_1
  N3: Part1.A2, R14.Pin_0, R15.pin_1
  N4: Part1.A3, R16.Pin_0, R17.pin_1
  N5: Part1.A4, R18.Pin_0, R19.pin_1
  N6: Part1.A5, R20.Pin_0, R21.pin_1
  N7: Part1.A6, R22.Pin_0, R23.pin_1
  N8: Part1.A7, R24.Pin_0, R25.pin_1
  N9: Part1.5V, R11.pin_0, R13.pin_0, R15.pin_0, R17.pin_0, R19.pin_0, R21.pin_0, R23.pin_0, R25.pin_0, LED1.anode, LED2.anode
  N10: Part1.GND, R10.Pin_1, R12.Pin_1, R14.Pin_1, R16.Pin_1, R18.Pin_1, R20.Pin_1, R22.Pin_1, R24.Pin_1, R26.Pin_1, R27.Pin_1
  N11: U1.+, U2.+, S1.COM
  N12: U1.-, U2.-, Stepdown_Voltage1.GND#2, DC_Mot_Enc5.pin4
  N13: Stepdown_Voltage1.VIn, DC_Mot_Enc5.pin5, S1.L1
  GND: Stepdown_Voltage1.GND#3, X1.GND, X4.GND, X6.GND, X7.GND, X10.GND
  N14: Stepdown_Voltage1.VOut, X1.VBUS, MD03A1.+5V_(IN), X4.VBUS, X6.VBUS, X7.VBUS, X10.D+
  N15: U4.P$1, X2.D+
  N16: U4.P$2, X2.VBUS
  N17: U4.D+, X2.GND
  N18: MD03A1.1INa, Part3.D50
  N19: MD03A1.1INb, Part3.D51
  N20: MD03A1.PWM, Part3.D7_PWM
  N21: MD03A1.GND, DC_Mot_Enc1.pin4, DC_Mot_Enc2.pin3, DC_Mot_Enc2.pin4, DC_Mot_Enc3.pin4, DC_Mot_Enc4.pin4, DC_Mot_Enc6.pin4, Part3.D20/SDA
  N22: MD03A1.2PWM, Part3.D6_PWM
  N23: MD03A1.2INb#142, Part3.D52
  N24: MD03A1.2INb#143, Part3.D53
  N25: MD03A1.OUT_1A, DC_Mot_Enc1.pin1, DC_Mot_Enc2.pin1, DC_Mot_Enc3.pin1
  N26: MD03A1.OUT_1B, DC_Mot_Enc1.pin2, DC_Mot_Enc2.pin2, DC_Mot_Enc3.pin2
  N27: MD03A1.OUT_2A, DC_Mot_Enc4.pin1, DC_Mot_Enc5.pin1, DC_Mot_Enc6.pin1
  N28: MD03A1.OUT_2B, DC_Mot_Enc4.pin2, DC_Mot_Enc5.pin2, DC_Mot_Enc6.pin2
  N29: MD03A1.VIN, DC_Mot_Enc1.pin5, DC_Mot_Enc2.pin5, DC_Mot_Enc3.pin5, DC_Mot_Enc4.pin5, DC_Mot_Enc6.pin5
  N30: X3.D-, X9.VBUS
  GND_2: X3.GND, X9.GND
  N31: X3.VBUS, X9.D+
  N32: DC_Mot_Enc1.pin3, Part3.D2_PWM
  N33: DC_Mot_Enc1.pin6, Part3.D4_PWM
  N34: DC_Mot_Enc2.pin6, Part3.D23
  N35: DC_Mot_Enc3.pin3, Part3.D18/TX1
  N36: DC_Mot_Enc3.pin6, Part3.D17_PWM/RX2
  N37: DC_Mot_Enc4.pin3, Part3.D3_PWM
  N38: DC_Mot_Enc4.pin6, Part3.D5_PWM
  N39: DC_Mot_Enc5.pin3, Part3.D21/SCL
  N40: DC_Mot_Enc5.pin6, Part3.D24
  N41: DC_Mot_Enc6.pin3, Part3.D19/RX1
  N42: DC_Mot_Enc6.pin6, Part3.D22
  N43: LED1.cathode, R26.Pin_0
  N44: LED2.cathode, R27.Pin_0

notes:
  7.4[V] Battery
  USB Hub
  Hokuyo
  7.4[V] to 5[V]
  Step-Down Voltage Regulator
  5[V] Source
  Motor Driver Shield
  M1
  M3
  M5
  M2
  M4
  M6
  Right Side Motors
  Left Side Motors
  On/Off Switch
  Lower level
  Upper level

custom parts:
  Polulu Stepdown Voltage: Polulu Stepdown Voltage 3V3 or 5V, 2.5A
  Toggle Switch spst: Toggle Switch single pole single throw
